// Logisim project cpu_1.circ as structural Verilog: 7 circuits, main circuit main
module main (
);

  wire Clock_out, cpu_1_read, cpu_1_write;
  wire [11:0] cpu_1_address_bus;
  wire [15:0] output_port_1_data_out, rom_1_data;

  Clock #(.highDuration(1), .lowDuration(1)) Clock (.out(Clock_out));
  LED led_1 (.in(Clock_out));
  CPU cpu_1 (
    .Write(cpu_1_write), .Read(cpu_1_read), .Clock(Clock_out), .Address_Bus(cpu_1_address_bus),
    .Data_Bus(rom_1_data));  // open: State
  ROM #(.addrWidth(12), .dataWidth(16)) rom_1 (.addr(cpu_1_address_bus), .data(rom_1_data));  // open: sel
  LED led_2 (.in(output_port_1_data_out[13]));
  LED led_3 (.in(output_port_1_data_out[14]));
  LED led_4 (.in(output_port_1_data_out[15]));
  LED led_5 (.in(output_port_1_data_out[9]));
  LED led_6 (.in(output_port_1_data_out[12]));
  LED led_7 (.in(output_port_1_data_out[10]));
  LED led_8 (.in(output_port_1_data_out[11]));
  Output_Port output_port_1 (
    .Data_Out(output_port_1_data_out), .Write(cpu_1_write), .Address_Bus(cpu_1_address_bus),
    .Port_s_Address(12'h3), .Data_Bus(rom_1_data));
  LED led_9 (.in(output_port_1_data_out[7]));
  LED led_10 (.in(output_port_1_data_out[8]));
  LED led_11 (.in(output_port_1_data_out[3]));
  LED led_12 (.in(output_port_1_data_out[4]));
  LED led_13 (.in(output_port_1_data_out[6]));
  LED led_14 (.in(output_port_1_data_out[5]));
  LED led_15 (.in(output_port_1_data_out[2]));
  LED led_16 (.in(output_port_1_data_out[0]));
  LED led_17 (.in(output_port_1_data_out[1]));

  // Notes on the sheet:
  //   contents of rom_1 (hex, n*v repeats v):
  //   8137 ac00 b000
endmodule

module CPU (
  input  Clock,
  input  [15:0] Data_Bus,
  output Write,
  output [3:0] State,
  output Read,
  output [11:0] Address_Bus
);

  wire alu_1_c_out, Carry_q, cpu_control_unit_1_acc__write, cpu_control_unit_1_address_mux,
       cpu_control_unit_1_alu_a_mux, cpu_control_unit_1_alu_op_mux, cpu_control_unit_1_carry_write,
       cpu_control_unit_1_data_write, cpu_control_unit_1_ir_write, cpu_control_unit_1_pc_write, not_1_out,
       or_1_out, or_2_out;
  wire [1:0] cpu_control_unit_1_acc__mux_low, cpu_control_unit_1_pc_mux_low;
  wire [3:0] multiplexer_6_out;
  wire [11:0] IR_q_2, multiplexer_1_out, PC_q;
  wire [15:0] Accumulator_q, alu_1_out, Data_q, multiplexer_3_out, multiplexer_4_out, multiplexer_5_out;
  wire [15:12] IR_q;

  Register #(.width(12), .trigger("rising")) PC (
    .D(multiplexer_1_out), .Q(PC_q), .clk(cpu_control_unit_1_pc_write));  // open: en, clr
  Multiplexer #(.select(2), .width(12)) multiplexer_1 (
    .in0(IR_q_2), .in1(alu_1_out[11:0]), .in2(Data_Bus[11:0]), .out(multiplexer_1_out),
    .sel(cpu_control_unit_1_pc_mux_low));  // open: in3
  Multiplexer #(.select(1), .width(12)) multiplexer_2 (
    .in0(IR_q_2), .in1(PC_q), .out(Address_Bus), .sel(cpu_control_unit_1_address_mux));
  Register #(.width(16), .trigger("rising")) IR (
    .D(Data_Bus), .Q({IR_q, IR_q_2}), .clk(cpu_control_unit_1_ir_write));  // open: en, clr
  CPU_Control_Unit cpu_control_unit_1 (
    .Clock(Clock), .Zero(not_1_out), .Minus(Accumulator_q[15]), .Carry(Carry_q), .Opcode(IR_q),
    .PC_MUX_Low(cpu_control_unit_1_pc_mux_low[0]), .PC_MUX_High(cpu_control_unit_1_pc_mux_low[1]),
    .PC_Write(cpu_control_unit_1_pc_write), .Address_MUX(cpu_control_unit_1_address_mux), .Write(Write),
    .Read(Read), .IR_Write(cpu_control_unit_1_ir_write), .Acc__MUX_Low(cpu_control_unit_1_acc__mux_low[0]),
    .Acc__MUX_High(cpu_control_unit_1_acc__mux_low[1]), .Acc__Write(cpu_control_unit_1_acc__write),
    .Data_Write(cpu_control_unit_1_data_write), .ALU_A_MUX(cpu_control_unit_1_alu_a_mux),
    .ALU_B_MUX(cpu_control_unit_1_alu_a_mux), .ALU_Op_MUX(cpu_control_unit_1_alu_op_mux),
    .Carry_Write(cpu_control_unit_1_carry_write), .State(State));
  assign Data_Bus = Write ? Accumulator_q : 16'bz;  // Controlled_Buffer controlled_buffer_1
  Multiplexer #(.select(2), .width(16)) multiplexer_3 (
    .in0(alu_1_out), .in1({4'b0000, IR_q_2}), .in2(Data_Bus), .out(multiplexer_3_out),
    .sel(cpu_control_unit_1_acc__mux_low));  // open: in3
  Register #(.width(16), .trigger("rising")) Accumulator (
    .D(multiplexer_3_out), .Q(Accumulator_q), .clk(cpu_control_unit_1_acc__write));  // open: en, clr
  Register #(.width(16), .trigger("rising")) Data (
    .D(Data_Bus), .Q(Data_q), .clk(cpu_control_unit_1_data_write));  // open: en, clr
  or or_1 (or_1_out, Accumulator_q[0], Accumulator_q[1], Accumulator_q[2], Accumulator_q[3], Accumulator_q[4], Accumulator_q[5], Accumulator_q[6], Accumulator_q[7], Accumulator_q[8]);
  or or_2 (or_2_out, or_1_out, Accumulator_q[9], Accumulator_q[10], Accumulator_q[11], Accumulator_q[12], Accumulator_q[13], Accumulator_q[14], Accumulator_q[15]);
  Multiplexer #(.select(1), .width(16)) multiplexer_4 (
    .in0(Accumulator_q), .in1({4'b0000, PC_q}), .out(multiplexer_4_out), .sel(cpu_control_unit_1_alu_a_mux));
  ALU alu_1 (
    .A(multiplexer_4_out), .B(multiplexer_5_out), .Op(multiplexer_6_out[2:0]), .C_In(Carry_q),
    .C_Out(alu_1_c_out), .Out(alu_1_out));
  Multiplexer #(.select(1), .width(16)) multiplexer_5 (
    .in0(Data_q), .in1(16'h1), .out(multiplexer_5_out), .sel(cpu_control_unit_1_alu_a_mux));
  D_Flip_Flop #(.trigger("rising")) Carry (
    .clk(cpu_control_unit_1_carry_write), .D(alu_1_c_out), .Q(Carry_q));  // open: Qn, preset, en, reset
  not not_1 (not_1_out, or_2_out);
  Multiplexer #(.select(1), .width(4)) multiplexer_6 (
    .in0(IR_q), .in1(4'b0000), .out(multiplexer_6_out), .sel(cpu_control_unit_1_alu_op_mux));
endmodule

module ALU (
  input  [2:0] Op,
  input  C_In,
  input  [15:0] A,
  input  [15:0] B,
  output [15:0] Out,
  output C_Out
);

  wire adder_2_cout, subtractor_2_bout;
  wire [15:0] adder_1_out, adder_2_out, and_1_out, not_1_out, or_1_out, subtractor_1_out, subtractor_2_out,
       xor_1_out;

  Adder #(.width(16)) adder_1 (.a(A), .b(B), .out(adder_1_out));  // open: cin, cout
  Subtractor #(.width(16)) subtractor_1 (.a(A), .b(B), .out(subtractor_1_out));  // open: bin, bout
  Adder #(.width(16)) adder_2 (.a(A), .b(B), .out(adder_2_out), .cin(C_In), .cout(adder_2_cout));
  Subtractor #(.width(16)) subtractor_2 (.a(A), .b(B), .out(subtractor_2_out), .bin(C_In), .bout(subtractor_2_bout));
  assign and_1_out = A & B;  // AND_Gate and_1, 16 bits wide
  assign or_1_out = A | B;  // OR_Gate or_1, 16 bits wide
  assign xor_1_out = A ^ B;  // XOR_Gate xor_1, 16 bits wide
  assign not_1_out = ~A;  // NOT_Gate not_1, 16 bits wide
  Multiplexer #(.select(3), .width(1)) multiplexer_1 (
    .in0(adder_2_cout), .in1(adder_2_cout), .in2(subtractor_2_bout), .in3(subtractor_2_bout), .out(C_Out),
    .sel(Op));  // open: in4, in5, in6, in7
  Multiplexer #(.select(3), .width(16)) multiplexer_2 (
    .in0(adder_1_out), .in1(adder_2_out), .in2(subtractor_1_out), .in3(subtractor_2_out), .in4(and_1_out),
    .in5(or_1_out), .in6(xor_1_out), .in7(not_1_out), .out(Out), .sel(Op));
endmodule

module CPU_Control_Unit (
  input  Clock,
  input  Zero,
  input  Minus,
  input  Carry,
  input  [3:0] Opcode,
  output [3:0] State,
  output PC_MUX_Low,
  output PC_Write,
  output Write,
  output IR_Write,
  output Acc__MUX_High,
  output Data_Write,
  output ALU_B_MUX,
  output Carry_Write,
  output PC_MUX_High,
  output Address_MUX,
  output Read,
  output Acc__MUX_Low,
  output Acc__Write,
  output ALU_A_MUX,
  output ALU_Op_MUX
);

  wire decoder_1_out3, decoder_1_out8, decoder_1_out9;
  wire [3:0] cpu_control_next_state_1_next_state;

  Decoder #(.select(4), .tristate("false")) decoder_1 (
    .out0(Address_MUX), .out2(Data_Write), .out3(decoder_1_out3), .out4(Carry_Write), .out5(Acc__MUX_Low),
    .out6(Acc__MUX_High), .out7(Write), .out8(decoder_1_out8), .out9(decoder_1_out9), .out10(PC_MUX_High),
    .sel(State));  // open: out1, out11, out12, out13, out14, out15
  or or_1 (PC_Write, Address_MUX, decoder_1_out9, PC_MUX_High);
  Register #(.width(4), .trigger("rising")) u_State (
    .D(cpu_control_next_state_1_next_state), .Q(State), .clk(Clock));  // open: en, clr
  not not_1 (Read, decoder_1_out8);
  CPU_Control_Next_State cpu_control_next_state_1 (
    .State(State), .Operation(Opcode), .Zero(Zero), .Minus(Minus), .Carry(Carry),
    .Next_State(cpu_control_next_state_1_next_state));
  or or_2 (Acc__Write, decoder_1_out3, Carry_Write, Acc__MUX_Low, Acc__MUX_High, Acc__MUX_High);

  assign ALU_A_MUX = Address_MUX;
  assign ALU_B_MUX = Address_MUX;
  assign ALU_Op_MUX = Address_MUX;
  assign IR_Write = Address_MUX;
  assign PC_MUX_Low = Address_MUX;
endmodule

module CPU_Control_Next_State (
  input  [3:0] State,
  input  [3:0] Operation,
  input  Zero,
  input  Minus,
  input  Carry,
  output [3:0] Next_State
);

  wire and_1_out, and_2_out, and_3_out, and_4_out, and_5_out, and_6_out, and_7_out, and_8_out, and_9_out,
       and_10_out, and_11_out, and_12_out, and_13_out, and_14_out, decoder_1_out0, decoder_1_out1,
       decoder_1_out2, decoder_1_out7, not_1_out, not_2_out, not_3_out, not_4_out;

  Decoder #(.select(4), .tristate("false")) decoder_1 (
    .out0(decoder_1_out0), .out1(decoder_1_out1), .out2(decoder_1_out2), .out7(decoder_1_out7), .sel(State));  // open: out3, out4, out5, out6, out8, out9, out10, out11, out12, out13, out14, out15
  not not_1 (not_1_out, Operation[3]);
  not not_2 (not_2_out, Operation[2]);
  not not_3 (not_3_out, Operation[2]);
  not not_4 (not_4_out, Operation[0]);
  and and_1 (and_1_out, decoder_1_out1, Operation[3], not_2_out, not_3_out);
  and and_2 (and_2_out, decoder_1_out1, Operation[3], not_2_out, Operation[2], Operation[0]);
  and and_3 (and_3_out, decoder_1_out1, Operation[3], Operation[2], not_3_out, Operation[0], Zero);
  and and_4 (and_4_out, decoder_1_out1, Operation[3], Operation[2], Operation[2], not_4_out, Minus);
  and and_5 (and_5_out, decoder_1_out1, Operation[3], Operation[2], Operation[2], Operation[0], Carry);
  and and_6 (and_6_out, decoder_1_out1, not_1_out, not_2_out);
  and and_7 (and_7_out, decoder_1_out2, not_1_out, not_2_out);
  and and_8 (and_8_out, decoder_1_out1, not_1_out, Operation[2], not_3_out);
  and and_9 (and_9_out, decoder_1_out1, Operation[3], not_2_out, not_3_out, Operation[0]);
  and and_10 (and_10_out, decoder_1_out1, Operation[3], not_2_out, Operation[2], not_4_out);
  and and_11 (and_11_out, decoder_1_out1, Operation[3], Operation[2], not_3_out, not_4_out);
  and and_12 (and_12_out, decoder_1_out2, not_1_out, Operation[2], not_3_out);
  and and_13 (and_13_out, decoder_1_out1, not_1_out, Operation[2], Operation[2], Operation[0]);
  and and_14 (and_14_out, decoder_1_out2, not_1_out, Operation[2], Operation[2], not_4_out);
  or or_1 (Next_State[0], decoder_1_out0, and_1_out, and_2_out, and_3_out, and_4_out, and_5_out, and_7_out);
  or or_2 (Next_State[1], and_7_out, and_6_out, and_8_out, and_9_out, and_10_out, and_11_out);
  or or_3 (Next_State[2], and_12_out, and_14_out, and_13_out, and_1_out);
  or or_4 (Next_State[3], decoder_1_out7, and_11_out, and_5_out, and_4_out, and_3_out, and_2_out);

  assign Operation[1] = Operation[2];
endmodule

module _8_bit_Toggle_Array (
  input  I0,
  input  I1,
  input  I2,
  input  I3,
  input  I4,
  input  I5,
  input  I6,
  input  I7,
  output O0,
  output O1,
  output O2,
  output O3,
  output O4,
  output O5,
  output O6,
  output O7
);

  wire d_ff_1_qn, d_ff_2_qn, d_ff_3_qn, d_ff_4_qn, d_ff_5_qn, d_ff_6_qn, d_ff_7_qn, d_ff_8_qn;

  D_Flip_Flop #(.trigger("rising")) d_ff_1 (
    .clk(I0), .D(d_ff_1_qn), .Q(O0), .Qn(d_ff_1_qn), .en(1'b1));  // open: preset, reset
  D_Flip_Flop #(.trigger("rising")) d_ff_2 (
    .clk(I1), .D(d_ff_2_qn), .Q(O1), .Qn(d_ff_2_qn), .en(1'b1));  // open: preset, reset
  D_Flip_Flop #(.trigger("rising")) d_ff_3 (
    .clk(I2), .D(d_ff_3_qn), .Q(O2), .Qn(d_ff_3_qn), .en(1'b1));  // open: preset, reset
  D_Flip_Flop #(.trigger("rising")) d_ff_4 (
    .clk(I3), .D(d_ff_4_qn), .Q(O3), .Qn(d_ff_4_qn), .en(1'b1));  // open: preset, reset
  D_Flip_Flop #(.trigger("rising")) d_ff_5 (
    .clk(I4), .D(d_ff_5_qn), .Q(O4), .Qn(d_ff_5_qn), .en(1'b1));  // open: preset, reset
  D_Flip_Flop #(.trigger("rising")) d_ff_6 (
    .clk(I5), .D(d_ff_6_qn), .Q(O5), .Qn(d_ff_6_qn), .en(1'b1));  // open: preset, reset
  D_Flip_Flop #(.trigger("rising")) d_ff_7 (
    .clk(I6), .D(d_ff_7_qn), .Q(O6), .Qn(d_ff_7_qn), .en(1'b1));  // open: preset, reset
  D_Flip_Flop #(.trigger("rising")) d_ff_8 (
    .clk(I7), .D(d_ff_8_qn), .Q(O7), .Qn(d_ff_8_qn), .en(1'b1));  // open: preset, reset
endmodule

module Output_Port (
  input  Write,
  input  [11:0] Address_Bus,
  input  [11:0] Port_s_Address,
  input  [15:0] Data_Bus,
  output [15:0] Data_Out
);

  wire and_1_out, and_2_out;
  wire [11:0] xnor_1_out;

  and and_1 (and_1_out, xnor_1_out[11], xnor_1_out[10], xnor_1_out[9], xnor_1_out[8], xnor_1_out[7], xnor_1_out[6], xnor_1_out[5], xnor_1_out[4], xnor_1_out[3]);
  assign xnor_1_out = ~(Address_Bus ^ Port_s_Address);  // XNOR_Gate xnor_1, 12 bits wide
  and and_2 (and_2_out, Write, and_1_out, xnor_1_out[2], xnor_1_out[1], xnor_1_out[0]);
  Register #(.width(16), .trigger("rising")) Port_Data (.D(Data_Bus), .Q(Data_Out), .clk(and_2_out));  // open: en, clr
endmodule
