// Logisim project cpu_2_bf.circ as structural Verilog: 16 circuits, main circuit main
module main (
);

  wire and_1_out, and_2_out, and_3_out, and_4_out, app_dotmover_1_out_6, clock_1_out, clock_2_out,
       counter_1_carry, cpu_1_read, cpu_1_write, not_1_out, not_2_out, not_3_out, not_4_out, not_5_out,
       or_1_out, or_2_out, output_port_3_write_enable, output_selector_1_write_enable,
       output_selector_2_write_enable, port_select_fromrange_1_select, port_select_fromrange_2_select,
       programdockcontroller_1_out_7, programdockcontroller_1_out_8, programdockcontroller_1_read_2,
       programdockcontroller_1_write_2, t_ff_1_q, t_ff_2_q, Toggle_Clock_out, Toggle_RAM_Loader_out, undriven;
  wire [0:0] output_port_1_data_out;
  wire [1:0] cpu_1_address_bus_2, joystick_1_x, joystick_1_y;
  wire [6:0] keyboard_1_data;
  wire [9:0] cpu_1_address_bus;
  wire [10:0] counter_1_q;
  wire [11:0] programdockcontroller_1_address_bus_2, programdockcontroller_1_ports_address, subtractor_1_out;
  wire [14:0] output_port_1_data_out_2, Quit_out;
  wire [15:0] app_dotmover_1_data_out, controlled_buffer_1_out, controlled_buffer_2_out,
       controlled_buffer_6_out, cpu_1_data_bus_out, KeyboardBuffer_q, n16x16_screen_controller_1_row,
       n16x16_screen_controller_1_row_2, n16x16_screen_controller_1_row_3, n16x16_screen_controller_1_row_4,
       n16x16_screen_controller_1_row_5, n16x16_screen_controller_1_row_6, n16x16_screen_controller_1_row_7,
       n16x16_screen_controller_1_row_8, n16x16_screen_controller_1_row_9, n16x16_screen_controller_1_row_10,
       n16x16_screen_controller_1_row_11, n16x16_screen_controller_1_row_12,
       n16x16_screen_controller_1_row_13, n16x16_screen_controller_1_row_14,
       n16x16_screen_controller_1_row_15, n16x16_screen_controller_1_row_16, output_port_2_data_out,
       output_port_3_data_out, output_port_4_data_out, output_port_5_data_out,
       programdockcontroller_1_data_in_2, ram_1_data, real_time_clock_1_hours, real_time_clock_1_minutes,
       real_time_clock_1_seconds, rom_1_data, shifter_1_out, shifter_2_out;

  Button Toggle_Clock (.out(Toggle_Clock_out));
  Clock clock_1 (.out(clock_1_out));
  and and_1 (and_1_out, clock_1_out, t_ff_1_q);
  CPU cpu_1 (
    .Read(cpu_1_read), .Write(cpu_1_write), .Clock(and_1_out),
    .Address_Bus({cpu_1_address_bus_2, cpu_1_address_bus}), .Data_Bus_Out(cpu_1_data_bus_out),
    .Data_Bus_In(controlled_buffer_2_out));
  LED led_1 (.in(t_ff_1_q));
  or or_1 (or_1_out, Toggle_Clock_out, and_2_out);
  T_Flip_Flop t_ff_1 (.clk(or_1_out), .T(or_1_out), .Q(t_ff_1_q));  // open: Qn, preset, reset, en
  assign controlled_buffer_1_out = not_1_out ? cpu_1_data_bus_out : 16'bz;  // Controlled_Buffer controlled_buffer_1
  assign controlled_buffer_2_out = cpu_1_read ? controlled_buffer_1_out : 16'bz;  // Controlled_Buffer controlled_buffer_2
  not not_1 (not_1_out, cpu_1_read);
  APP_HelloWorld app_helloworld_1 ();  // open: Read, Write, Data_In, Data_Out, Address_Bus, Ports_Address, out_6
  Subtractor #(.width(12)) subtractor_1 (
    .a({cpu_1_address_bus_2, cpu_1_address_bus}), .b(12'h400), .out(subtractor_1_out));  // open: bin, bout
  APP_SpaceInvaders app_spaceinvaders_1 ();  // open: Read, Write, Data_In, Data_Out, Address_Bus, Ports_Address, out_6
  Port_Select_fromRange port_select_fromrange_1 (
    .Select(port_select_fromrange_1_select), .Address_Bus({cpu_1_address_bus_2, cpu_1_address_bus}),
    .Range_LOW(12'h1), .Range_HIGH(12'h3ff));
  Port_Select_fromRange port_select_fromrange_2 (
    .Select(port_select_fromrange_2_select), .Address_Bus({cpu_1_address_bus_2, cpu_1_address_bus}),
    .Range_LOW(12'h400), .Range_HIGH(12'hbff));
  RAM #(.addrWidth(10), .dataWidth(16)) ram_1 (
    .addr(cpu_1_address_bus), .data(ram_1_data), .sel(port_select_fromrange_1_select), .clk(cpu_1_write),
    .ld(cpu_1_read));  // open: clr
  assign ram_1_data = not_4_out ? controlled_buffer_1_out : 16'bz;  // Controlled_Buffer controlled_buffer_3
  assign controlled_buffer_1_out = cpu_1_read ? ram_1_data : 16'bz;  // Controlled_Buffer controlled_buffer_4
  assign controlled_buffer_1_out = cpu_1_read ? controlled_buffer_6_out : 16'bz;  // Controlled_Buffer controlled_buffer_5
  assign controlled_buffer_6_out = not_2_out ? controlled_buffer_1_out : 16'bz;  // Controlled_Buffer controlled_buffer_6
  RAM #(.addrWidth(11), .dataWidth(16)) ram_2 (
    .addr(subtractor_1_out[10:0]), .data(controlled_buffer_6_out), .sel(port_select_fromrange_2_select),
    .clk(cpu_1_write), .ld(cpu_1_read), .clr(undriven));
  not not_2 (not_2_out, cpu_1_read);
  and and_2 (and_2_out, output_port_1_data_out[0], not_3_out);
  not not_3 (not_3_out, output_port_1_data_out[0]);
  Output_Port output_port_1 (
    .Data_Out({output_port_1_data_out_2, output_port_1_data_out[0]}), .Write(cpu_1_write),
    .Address_Bus({cpu_1_address_bus_2, cpu_1_address_bus}), .Port_s_Address(12'hc09),
    .Data_Bus(controlled_buffer_1_out));  // open: Write_Enable
  not not_4 (not_4_out, cpu_1_read);
  Input_Port input_port_1 (
    .Data_Bus(controlled_buffer_1_out), .Read(cpu_1_read),
    .Address_Bus({cpu_1_address_bus_2, cpu_1_address_bus}), .Port_s_Address(12'hc00),
    .Data_In({{14{1'b0}}, joystick_1_x}));
  Input_Port input_port_2 (
    .Data_Bus(controlled_buffer_1_out), .Read(cpu_1_read),
    .Address_Bus({cpu_1_address_bus_2, cpu_1_address_bus}), .Port_s_Address({12{1'b0}}), .Data_In(16'hb400));
  _16x16_screen_controller u_16x16_screen_controller_1 (
    .Row_Data(output_port_3_data_out), .Row_Select(output_port_2_data_out),
    .Write(output_port_3_write_enable), .Row(n16x16_screen_controller_1_row),
    .Row_2(n16x16_screen_controller_1_row_2), .Row_3(n16x16_screen_controller_1_row_3),
    .Row_4(n16x16_screen_controller_1_row_4), .Row_5(n16x16_screen_controller_1_row_5),
    .Row_6(n16x16_screen_controller_1_row_6), .Row_7(n16x16_screen_controller_1_row_7),
    .Row_8(n16x16_screen_controller_1_row_8), .Row_9(n16x16_screen_controller_1_row_9),
    .Row_10(n16x16_screen_controller_1_row_10), .Row_11(n16x16_screen_controller_1_row_11),
    .Row_12(n16x16_screen_controller_1_row_12), .Row_13(n16x16_screen_controller_1_row_13),
    .Row_14(n16x16_screen_controller_1_row_14), .Row_15(n16x16_screen_controller_1_row_15),
    .Row_16(n16x16_screen_controller_1_row_16));
  DotMatrix #(.inputtype("row"), .matrixcols(16), .matrixrows(16)) dotmatrix_1 (
    .row0(n16x16_screen_controller_1_row), .row1(n16x16_screen_controller_1_row_2),
    .row2(n16x16_screen_controller_1_row_3), .row3(n16x16_screen_controller_1_row_4),
    .row4(n16x16_screen_controller_1_row_5), .row5(n16x16_screen_controller_1_row_6),
    .row6(n16x16_screen_controller_1_row_7), .row7(n16x16_screen_controller_1_row_8),
    .row8(n16x16_screen_controller_1_row_9), .row9(n16x16_screen_controller_1_row_10),
    .row10(n16x16_screen_controller_1_row_11), .row11(n16x16_screen_controller_1_row_12),
    .row12(n16x16_screen_controller_1_row_13), .row13(n16x16_screen_controller_1_row_14),
    .row14(n16x16_screen_controller_1_row_15), .row15(n16x16_screen_controller_1_row_16));
  Output_Port output_port_2 (
    .Data_Out(output_port_2_data_out), .Write(cpu_1_write),
    .Address_Bus({cpu_1_address_bus_2, cpu_1_address_bus}), .Port_s_Address(12'hc00),
    .Data_Bus(controlled_buffer_1_out));  // open: Write_Enable
  Joystick #(.bits(2)) joystick_1 (.x(joystick_1_x), .y(joystick_1_y));
  Clock clock_2 (.out(clock_2_out));
  or or_2 (or_2_out, counter_1_carry, Toggle_RAM_Loader_out);
  and and_3 (and_3_out, clock_2_out, t_ff_2_q);
  Output_Port output_port_3 (
    .Data_Out(output_port_3_data_out), .Write(cpu_1_write),
    .Address_Bus({cpu_1_address_bus_2, cpu_1_address_bus}), .Port_s_Address(12'hc01),
    .Data_Bus(controlled_buffer_1_out), .Write_Enable(output_port_3_write_enable));
  Input_Port input_port_3 (
    .Data_Bus(controlled_buffer_1_out), .Read(cpu_1_read),
    .Address_Bus({cpu_1_address_bus_2, cpu_1_address_bus}), .Port_s_Address(12'hc01),
    .Data_In({{14{1'b0}}, joystick_1_y}));
  LED led_2 (.in(t_ff_2_q));
  Button Toggle_RAM_Loader (.out(Toggle_RAM_Loader_out));
  T_Flip_Flop t_ff_2 (.clk(or_2_out), .T(or_2_out), .Q(t_ff_2_q));  // open: Qn, preset, reset, en
  Counter #(.width(11), .max('h7ff), .trigger("falling")) counter_1 (
    .count(1'b1), .Q(counter_1_q), .carry(counter_1_carry), .clk(and_3_out), .clr(Toggle_RAM_Loader_out));  // open: load, D
  TTY #(.rows(16), .cols(64)) tty_1 (
    .data(controlled_buffer_1_out[6:0]), .clk(output_selector_1_write_enable),
    .we(output_selector_1_write_enable), .clr(and_2_out));
  Output_Selector output_selector_1 (
    .Write_Enable(output_selector_1_write_enable), .Write(cpu_1_write),
    .Address_Bus({cpu_1_address_bus_2, cpu_1_address_bus}), .Port_s_Address(12'hc02));
  Output_Selector output_selector_2 (
    .Write_Enable(output_selector_2_write_enable), .Write(and_4_out),
    .Address_Bus({cpu_1_address_bus_2, cpu_1_address_bus}), .Port_s_Address(12'hc02));
  assign controlled_buffer_1_out = output_selector_2_write_enable ? KeyboardBuffer_q : 16'bz;  // Controlled_Buffer controlled_buffer_7
  Register #(.width(16)) KeyboardBuffer (
    .D({{9{1'b0}}, keyboard_1_data}), .Q(KeyboardBuffer_q), .clk(output_selector_2_write_enable));  // open: en, clr
  Keyboard #(.buflen(128)) keyboard_1 (
    .clk(output_selector_2_write_enable), .data(keyboard_1_data));  // open: re, clr, avail
  and and_4 (and_4_out, cpu_1_read, not_5_out);
  ROM #(.addrWidth(11), .dataWidth(16)) rom_1 (.addr(counter_1_q), .data(rom_1_data));  // open: sel
  not not_5 (not_5_out, and_1_out);
  ProgramDockController programdockcontroller_1 (
    .Read(cpu_1_read), .Write(cpu_1_write), .Data_In(controlled_buffer_1_out),
    .Data_Out_2(controlled_buffer_1_out), .Address_Bus({cpu_1_address_bus_2, cpu_1_address_bus}),
    .out_7(programdockcontroller_1_out_7), .out_8(programdockcontroller_1_out_8),
    .Read_2(programdockcontroller_1_read_2), .Write_2(programdockcontroller_1_write_2),
    .Data_In_2(programdockcontroller_1_data_in_2), .Data_Out(app_dotmover_1_data_out),
    .Address_Bus_2(programdockcontroller_1_address_bus_2),
    .Ports_Address(programdockcontroller_1_ports_address), .in_6(app_dotmover_1_out_6));
  LED led_3 (.in(programdockcontroller_1_out_7));
  LED led_4 (.in(programdockcontroller_1_out_8));
  APP_DotMover app_dotmover_1 (
    .Read(programdockcontroller_1_read_2), .Write(programdockcontroller_1_write_2),
    .Data_In(programdockcontroller_1_data_in_2), .Data_Out(app_dotmover_1_data_out),
    .Address_Bus(programdockcontroller_1_address_bus_2),
    .Ports_Address(programdockcontroller_1_ports_address), .out_6(app_dotmover_1_out_6));
  Input_Port input_port_4 (
    .Data_Bus(controlled_buffer_1_out), .Read(cpu_1_read),
    .Address_Bus({cpu_1_address_bus_2, cpu_1_address_bus}), .Port_s_Address(12'hc04),
    .Data_In(real_time_clock_1_hours));
  Input_Port input_port_5 (
    .Data_Bus(controlled_buffer_1_out), .Read(cpu_1_read),
    .Address_Bus({cpu_1_address_bus_2, cpu_1_address_bus}), .Port_s_Address(12'hc05),
    .Data_In(real_time_clock_1_minutes));
  Real_Time_Clock real_time_clock_1 (
    .Clock(and_1_out), .Hours(real_time_clock_1_hours), .Minutes(real_time_clock_1_minutes),
    .Seconds(real_time_clock_1_seconds));  // open: SetSeconds, SetMinutes, SetHours, Set
  Button Quit (.out(Quit_out[0]));
  Button Previous (.out(Quit_out[2]));
  Button Next (.out(Quit_out[4]));
  Button Select (.out(Quit_out[6]));
  Button Yes (.out(Quit_out[8]));
  Button No (.out(Quit_out[10]));
  Button button_1 (.out(Quit_out[12]));
  Button button_2 (.out(Quit_out[14]));
  Input_Port input_port_6 (
    .Data_Bus(controlled_buffer_1_out), .Read(cpu_1_read),
    .Address_Bus({cpu_1_address_bus_2, cpu_1_address_bus}), .Port_s_Address(12'hc09),
    .Data_In({1'b0, Quit_out[14], 1'b0, Quit_out[12], 1'b0, Quit_out[10], 1'b0, Quit_out[8], 1'b0, Quit_out[6], 1'b0, Quit_out[4], 1'b0, Quit_out[2], 1'b0, Quit_out[0]}));
  Input_Port input_port_7 (
    .Data_Bus(controlled_buffer_1_out), .Read(cpu_1_read),
    .Address_Bus({cpu_1_address_bus_2, cpu_1_address_bus}), .Port_s_Address(12'hc06),
    .Data_In(real_time_clock_1_seconds));
  Input_Port input_port_8 (
    .Data_Bus(controlled_buffer_1_out), .Read(cpu_1_read),
    .Address_Bus({cpu_1_address_bus_2, cpu_1_address_bus}), .Port_s_Address(12'hc07), .Data_In(shifter_1_out));
  Shifter #(.width(16), .shift("rl")) shifter_1 (.in(output_port_4_data_out), .\dist (4'b0001), .out(shifter_1_out));
  Output_Port output_port_4 (
    .Data_Out(output_port_4_data_out), .Write(cpu_1_write),
    .Address_Bus({cpu_1_address_bus_2, cpu_1_address_bus}), .Port_s_Address(12'hc07),
    .Data_Bus(controlled_buffer_1_out));  // open: Write_Enable
  Input_Port input_port_9 (
    .Data_Bus(controlled_buffer_1_out), .Read(cpu_1_read),
    .Address_Bus({cpu_1_address_bus_2, cpu_1_address_bus}), .Port_s_Address(12'hc08), .Data_In(shifter_2_out));
  Shifter #(.width(16), .shift("rr")) shifter_2 (.in(output_port_5_data_out), .\dist (4'b0001), .out(shifter_2_out));
  Output_Port output_port_5 (
    .Data_Out(output_port_5_data_out), .Write(cpu_1_write),
    .Address_Bus({cpu_1_address_bus_2, cpu_1_address_bus}), .Port_s_Address(12'hc08),
    .Data_Bus(controlled_buffer_1_out));  // open: Write_Enable

  // Notes on the sheet:
  //   CPU
  //   Pixel Mover
  //   Hello World
  //   1K PROGRAM RAM
  //   2K RAM
  //   Space Invaders
  //   Start Address
  //   16x16 Pixel Display
  //   Joystick
  //   ASCII Keyboard Input
  //   contents of rom_1 (hex, n*v repeats v):
  //   b95c 16*0 3e 20 0 2a 0 3a 0 d c 32*0 44 72 65 77 0 31 32 33 34 0 30 6*0 a 8 1 4 10 40 100 400 74 69
  //   6d 65 0 72 61 6e 64 0 63 6c 65 61 72 0 68 61 6c 74 0 65 63 68 6f 0 6c 6f 61 64 0 453 458 45d 463 468
  //   46d 7f2 820 832 839 853 866 5 5 6 5 4 5 b488 0 9000 b000 848b a988 b993 a485 848f a988 b993 486 a491
  //   9000 d498 ac02 9491 986 a491 b491 800d ac02 c485 b49e 0 9000 84a1 a988 b993 a49c 84a5 a988 b993 49d
  //   a4a7 9000 d4ae ac02 94a7 986 a4a7 b4a7 c49c b4c7 c 57 65 6c 63 6f 6d 65 20 74 6f 20 44 72 65 77 4f
  //   53 21 0 472 43a 43f 8478 24c4 a448 843f 24c5 2986 a449 8444 24c6 2986 a44a 84b0 a987 84d7 a988 b989
  //   84dd a987 84dc a988 b989 b484 84e0 a988 b993 a99b c99b b54a 0 55 73 65 72 6e 61 6d 65 3a 20 0 50 61
  //   73 73 77 6f 72 64 3a 20 0 59 6f 75 20 61 72 65 20 6e 6f 77 20 6c 6f 67 67 65 64 20 69 6e 20 61 73 20
  //   0 49 6e 63 6f 72 72 65 63 74 20 75 73 65 72 6e 61 6d 65 20 2f 20 70 61 73 73 77 6f 72 64 25*0 854d
  //   a988 b993 a4e3 943a d5f3 943f d5f3 84e4 a987 8557 a988 b989 855d a987 855c a988 b989 b49b 8000 a549
  //   9c02 d55f a532 644b d572 800a 2549 d55f 9549 986 a549 9532 a533 956b 986 a56b 9532 ac02 b55f 9418
  //   ac02 84ef a987 8579 a988 b989 857f a987 857e a988 b989 b49b 8000 a549 9c02 d581 a532 644b d594 800a
  //   2549 d581 9549 986 a549 9532 a53e 958d 986 a58d 9414 ac02 b581 9533 d5a0 643a d599 b5c5 9594 986
  //   a594 9596 986 a596 b594 953e d5ac 643f d5a5 b5c5 95a0 986 a5a0 95a2 986 a5a2 b5a0 9418 ac02 84fa
  //   a987 85b3 a988 b989 85b9 a987 85b8 a988 b989 b49b 843a a987 85be a988 b989 85c4 a987 85c3 a988 b989
  //   b484 b5f3 9418 ac02 8514 a987 85cc a988 b989 85d2 a987 85d1 a988 b989 b484 8533 a987 85d7 a988 b989
  //   800a a987 85dc a988 b989 85e2 a987 85e1 a988 b989 b5f4 853e a987 85e7 a988 b989 800a a987 85ec a988
  //   b989 85f2 a987 85f1 a988 b989 b5f4 b552 c4e3 b5f8 0 0 a000 85fb a988 b993 a5f5 85ff a988 b993 a5f6
  //   8603 a988 b993 5f7 a608 95f6 d610 8000 a000 95f6 2986 a5f6 9608 986 a608 b605 c5f5 b61f 0 0 2710 3e8
  //   64 a 1 0 0 2614 5 0 0 8622 a988 b993 a612 8626 a988 b993 a613 8000 a61a 961b a630 8005 a61c 8000
  //   a61e 9613 2614 e637 a613 961a 986 a61a b62f 961a a61d 961d 61e d643 961d d640 8fff a61e 961d 444
  //   ac02 9613 8000 a61a 9630 986 a630 961c 2986 a61c d65a b62f 8005 a61c 8653 a988 b993 444 ac02 961c
  //   2986 a61c d65a b650 c612 b660 4*0 8663 a988 b993 a65c 8667 a988 b993 a65d 866b a988 b993 a65e 8000
  //   a65f 965e d677 965f 65d a65f 965e 2986 a65e b66e 965f a987 867c a988 b989 c65c b689 0 0 0 2710 3e8
  //   64 a 1 0 5 2681 868c a988 b993 a67e 8690 a988 b993 a680 a687 8695 a988 b993 a67f 8005 2680 a680 9688
  //   a69f 9688 680 a69f 967f 2681 e6a2 b6a4 8030 ac02 969f 986 a69f 9687 2986 a687 d6ac b69e c67e b6b1 0
  //   0 0 9c06 a6ae 9c05 a6af 9c04 a6b0 96b0 a987 86bc a988 b989 8002 a987 86c1 a988 b989 86c7 a987 86c6
  //   a988 b989 b67d 96b0 a987 86cc a988 b989 86d2 a987 86d1 a988 b989 b611 9416 ac02 96af a987 86d9 a988
  //   b989 8002 a987 86de a988 b989 86e4 a987 86e3 a988 b989 b67d 96af a987 86e9 a988 b989 86ef a987 86ee
  //   a988 b989 b611 9416 ac02 96ae a987 86f6 a988 b989 8002 a987 86fb a988 b989 8701 a987 8700 a988 b989
  //   b67d 96ae a987 8706 a988 b989 870c a987 870b a988 b989 b611 870f a988 b993 a99b c99b b718 a41a 0 1e
  //   1e 2 1 9712 a74b 9715 a714 8000 a439 8411 a987 8723 a988 b989 8729 a987 8728 a988 b989 b49b 8001
  //   a717 9c02 d729 a713 644b d754 9713 644c d734 b743 8000 a717 9714 6715 d743 974b 2986 a74b 9714 a714
  //   944c ac02 9439 2986 a439 9717 d729 9714 2986 a714 d729 e729 9713 a41a ac02 9439 986 a439 974b 986
  //   a74b b729 9418 ac02 8759 a988 b993 a99b c99b b772 0 1 9000 c000 55 6e 6b 6e 6f 77 6e 20 63 6f 6d 6d
  //   61 6e 64 3a 20 0 8775 a988 b993 a75c 8472 75e a782 847e 75e a787 8478 75f a7a9 8001 9448 a75d 9472
  //   a987 8787 a988 b989 947e a987 878c a988 b989 8792 a987 8791 a988 b989 b7c1 8795 a988 b993 d7a4 975d
  //   2986 a75d d7aa 9787 986 a787 97a9 986 a7a9 9782 986 a782 b782 975c a987 87a9 a988 b989 c478 8760
  //   a987 87af a988 b989 87b5 a987 87b4 a988 b989 b49b 841a a987 87ba a988 b989 87c0 a987 87bf a988 b989
  //   b484 c75c b7c7 0 941a 6000 0 4 87ca a988 b993 a7c2 87ce a988 b993 a7c6 97c3 a7d6 87d4 a988 b993 7c4
  //   a7d8 941a a7c5 6453 d7db b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
  //   ASCII Terminal Output
  //   Cartridge Slot
  //   Elapsed-Time Clock
  //   Roll left / right
endmodule

module CPU (
  input  Clock,
  input  [15:0] Data_Bus_In,
  output [11:0] Address_Bus,
  output Read,
  output Write,
  output [15:0] Data_Bus_Out
);

  wire alu_1_c_out, and_2_out, Carry_q, cpu_control_1_acc_write, cpu_control_1_address_src_mux,
       cpu_control_1_data_write, cpu_control_1_ir_write, cpu_control_1_pc_write, cpu_control_1_write,
       nor_1_out, nor_2_out, not_1_out;
  wire [1:0] cpu_control_1_acc_src_mux, cpu_control_1_pc_src_mux;
  wire [3:0] controlled_buffer_1_out_2;
  wire [11:0] adder_1_out, controlled_buffer_1_out, IR_q, multiplexer_1_out, PC_Buffer_q, PC_q,
       subtractor_1_out, subtractor_2_out;
  wire [15:0] Acc__Buffer_q, Accumulator_q, alu_1_out, Data_q, multiplexer_2_out;
  wire [15:12] IR_q_2;

  Subtractor #(.width(12)) subtractor_1 (
    .a(controlled_buffer_1_out), .b(12'h1), .out(subtractor_1_out));  // open: bin, bout
  Multiplexer #(.select(2), .width(12), .enable("false")) multiplexer_1 (
    .in0(subtractor_2_out), .in1(PC_Buffer_q), .in2(subtractor_1_out), .out(multiplexer_1_out),
    .sel(cpu_control_1_pc_src_mux));  // open: in3
  and and_1 (Write, cpu_control_1_write, not_1_out);
  Subtractor #(.width(12)) subtractor_2 (.a(IR_q), .b(12'h1), .out(subtractor_2_out));  // open: bin, bout
  Register #(.width(12), .trigger("high")) PC (
    .D(multiplexer_1_out), .Q(PC_q), .clk(cpu_control_1_pc_write));  // open: en, clr
  not not_1 (not_1_out, Clock);
  Register #(.width(12)) PC_Buffer (
    .D(adder_1_out), .Q(PC_Buffer_q), .clk(cpu_control_1_pc_src_mux[0]));  // open: en, clr
  Adder #(.width(12)) adder_1 (.a(PC_q), .b(12'h1), .out(adder_1_out));  // open: cin, cout
  Register #(.width(16)) Acc__Buffer (
    .D(alu_1_out), .Q(Acc__Buffer_q), .clk(cpu_control_1_acc_write));  // open: en, clr
  Register #(.width(16), .trigger("high")) IR (
    .D({controlled_buffer_1_out_2, controlled_buffer_1_out}), .Q({IR_q_2, IR_q}), .clk(cpu_control_1_ir_write));  // open: en, clr
  Multiplexer #(.select(2), .width(16), .enable("false")) multiplexer_2 (
    .in0({4'b0000, IR_q}), .in1({controlled_buffer_1_out_2, controlled_buffer_1_out}), .in2(Acc__Buffer_q),
    .out(multiplexer_2_out), .sel(cpu_control_1_acc_src_mux));  // open: in3
  CPU_Control cpu_control_1 (
    .Clock(Clock), .Opcode(IR_q_2), .Zero(and_2_out), .Minus(Accumulator_q[15]), .Carry(Carry_q),
    .PC_Src_MUX(cpu_control_1_pc_src_mux[0]), .PC_Write(cpu_control_1_pc_write),
    .IR_Write(cpu_control_1_ir_write), .Data_Write(cpu_control_1_data_write),
    .Acc_Src_MUX(cpu_control_1_acc_src_mux), .Acc_Write(cpu_control_1_acc_write),
    .Write(cpu_control_1_write), .Address_Src_MUX(cpu_control_1_address_src_mux),
    .PC_Src_MUX_High(cpu_control_1_pc_src_mux[1]), .Read(Read));
  Register #(.width(16), .trigger("high")) Accumulator (
    .D(multiplexer_2_out), .Q(Accumulator_q), .clk(cpu_control_1_acc_write));  // open: en, clr
  Register #(.width(16), .trigger("high")) Data (
    .D({controlled_buffer_1_out_2, controlled_buffer_1_out}), .Q(Data_q), .clk(cpu_control_1_data_write));  // open: en, clr
  assign {controlled_buffer_1_out_2, controlled_buffer_1_out} = cpu_control_1_write ? Accumulator_q : 16'bz;  // Controlled_Buffer controlled_buffer_1
  ALU alu_1 (.A(Accumulator_q), .B(Data_q), .Op(IR_q_2[14:12]), .C_In(Carry_q), .C_Out(alu_1_c_out), .Out(alu_1_out));
  Multiplexer #(.width(12), .enable("false")) multiplexer_3 (
    .in0(PC_q), .in1(IR_q), .out(Address_Bus), .sel(cpu_control_1_address_src_mux));
  assign Data_Bus_In = cpu_control_1_write ? {controlled_buffer_1_out_2, controlled_buffer_1_out} : 16'bz;  // Controlled_Buffer controlled_buffer_2
  assign {controlled_buffer_1_out_2, controlled_buffer_1_out} = Read ? Data_Bus_In : 16'bz;  // Controlled_Buffer controlled_buffer_3
  Register #(.width(1)) Carry (.D(alu_1_c_out), .Q(Carry_q), .clk(Clock));  // open: en, clr
  nor nor_1 (nor_1_out, Accumulator_q[0], Accumulator_q[1], Accumulator_q[2], Accumulator_q[3], Accumulator_q[4], Accumulator_q[5], Accumulator_q[6], Accumulator_q[7], Accumulator_q[8]);
  nor nor_2 (nor_2_out, Accumulator_q[9], Accumulator_q[10], Accumulator_q[11], Accumulator_q[12], Accumulator_q[13], Accumulator_q[14], Accumulator_q[15]);
  and and_2 (and_2_out, nor_1_out, nor_2_out);

  assign Data_Bus_Out = Data_Bus_In;

  // Notes on the sheet:
  //   PC Src Multiplexer
  //   Acc. Src MUX
  //   ALU
  //   Address Src Multiplexer
endmodule

module ALU (
  input  [2:0] Op,
  input  C_In,
  input  [15:0] A,
  input  [15:0] B,
  output [15:0] Out,
  output C_Out
);

  wire adder_2_cout, subtractor_2_bout;
  wire [15:0] adder_1_out, adder_2_out, and_1_out, not_1_out, or_1_out, subtractor_1_out, subtractor_2_out,
       xor_1_out;

  Adder #(.width(16)) adder_1 (.a(A), .b(B), .out(adder_1_out));  // open: cin, cout
  Subtractor #(.width(16)) subtractor_1 (.a(A), .b(B), .out(subtractor_1_out));  // open: bin, bout
  Adder #(.width(16)) adder_2 (.a(A), .b(B), .out(adder_2_out), .cin(C_In), .cout(adder_2_cout));
  Subtractor #(.width(16)) subtractor_2 (.a(A), .b(B), .out(subtractor_2_out), .bin(C_In), .bout(subtractor_2_bout));
  assign and_1_out = A & B;  // AND_Gate and_1, 16 bits wide
  assign or_1_out = A | B;  // OR_Gate or_1, 16 bits wide
  assign xor_1_out = A ^ B;  // XOR_Gate xor_1, 16 bits wide
  assign not_1_out = ~A;  // NOT_Gate not_1, 16 bits wide
  Multiplexer #(.select(3), .enable("false")) multiplexer_1 (
    .in0(adder_2_cout), .in1(adder_2_cout), .in2(subtractor_2_bout), .in3(subtractor_2_bout), .out(C_Out),
    .sel(Op));  // open: in4, in5, in6, in7
  Multiplexer #(.select(3), .width(16), .enable("false")) multiplexer_2 (
    .in0(adder_1_out), .in1(adder_2_out), .in2(subtractor_1_out), .in3(subtractor_2_out), .in4(and_1_out),
    .in5(or_1_out), .in6(xor_1_out), .in7(not_1_out), .out(Out), .sel(Op));
endmodule

module Input_Port (
  input  Read,
  input  [11:0] Address_Bus,
  input  [11:0] Port_s_Address,
  input  [15:0] Data_In,
  output [15:0] Data_Bus
);

  wire and_1_out, and_2_out;
  wire [11:0] xnor_1_out;

  and and_1 (and_1_out, xnor_1_out[11], xnor_1_out[10], xnor_1_out[9], xnor_1_out[8], xnor_1_out[7], xnor_1_out[6], xnor_1_out[5], xnor_1_out[4], xnor_1_out[3]);
  assign xnor_1_out = ~(Address_Bus ^ Port_s_Address);  // XNOR_Gate xnor_1, 12 bits wide
  and and_2 (and_2_out, Read, and_1_out, xnor_1_out[2], xnor_1_out[1], xnor_1_out[0]);
  assign Data_Bus = and_2_out ? Data_In : 16'bz;  // Controlled_Buffer controlled_buffer_1
endmodule

module Output_Port (
  input  Write,
  input  [11:0] Address_Bus,
  input  [11:0] Port_s_Address,
  input  [15:0] Data_Bus,
  output [15:0] Data_Out,
  output Write_Enable
);

  wire and_1_out;
  wire [11:0] xnor_1_out;

  and and_1 (and_1_out, xnor_1_out[11], xnor_1_out[10], xnor_1_out[9], xnor_1_out[8], xnor_1_out[7], xnor_1_out[6], xnor_1_out[5], xnor_1_out[4], xnor_1_out[3]);
  assign xnor_1_out = ~(Address_Bus ^ Port_s_Address);  // XNOR_Gate xnor_1, 12 bits wide
  and and_2 (Write_Enable, Write, and_1_out, xnor_1_out[2], xnor_1_out[1], xnor_1_out[0]);
  Register #(.width(16)) Port_Data (.D(Data_Bus), .Q(Data_Out), .clk(Write_Enable));  // open: en, clr
endmodule

module Output_Selector (
  input  Write,
  input  [11:0] Address_Bus,
  input  [11:0] Port_s_Address,
  output Write_Enable
);

  wire and_1_out;
  wire [11:0] xnor_1_out;

  and and_1 (and_1_out, xnor_1_out[11], xnor_1_out[10], xnor_1_out[9], xnor_1_out[8], xnor_1_out[7], xnor_1_out[6], xnor_1_out[5], xnor_1_out[4], xnor_1_out[3]);
  assign xnor_1_out = ~(Address_Bus ^ Port_s_Address);  // XNOR_Gate xnor_1, 12 bits wide
  and and_2 (Write_Enable, Write, and_1_out, xnor_1_out[2], xnor_1_out[1], xnor_1_out[0]);
endmodule

module _8_bit_Toggle_Array (
  input  I0,
  input  I1,
  input  I2,
  input  I3,
  input  I4,
  input  I5,
  input  I6,
  input  I7,
  output O0,
  output O1,
  output O2,
  output O3,
  output O4,
  output O5,
  output O6,
  output O7
);

  wire d_ff_1_qn, d_ff_2_qn, d_ff_3_qn, d_ff_4_qn, d_ff_5_qn, d_ff_6_qn, d_ff_7_qn, d_ff_8_qn;

  D_Flip_Flop d_ff_1 (.clk(I0), .D(d_ff_1_qn), .Q(O0), .Qn(d_ff_1_qn), .en(1'b1));  // open: preset, reset
  D_Flip_Flop d_ff_2 (.clk(I1), .D(d_ff_2_qn), .Q(O1), .Qn(d_ff_2_qn), .en(1'b1));  // open: preset, reset
  D_Flip_Flop d_ff_3 (.clk(I2), .D(d_ff_3_qn), .Q(O2), .Qn(d_ff_3_qn), .en(1'b1));  // open: preset, reset
  D_Flip_Flop d_ff_4 (.clk(I3), .D(d_ff_4_qn), .Q(O3), .Qn(d_ff_4_qn), .en(1'b1));  // open: preset, reset
  D_Flip_Flop d_ff_5 (.clk(I4), .D(d_ff_5_qn), .Q(O4), .Qn(d_ff_5_qn), .en(1'b1));  // open: preset, reset
  D_Flip_Flop d_ff_6 (.clk(I5), .D(d_ff_6_qn), .Q(O5), .Qn(d_ff_6_qn), .en(1'b1));  // open: preset, reset
  D_Flip_Flop d_ff_7 (.clk(I6), .D(d_ff_7_qn), .Q(O6), .Qn(d_ff_7_qn), .en(1'b1));  // open: preset, reset
  D_Flip_Flop d_ff_8 (.clk(I7), .D(d_ff_8_qn), .Q(O7), .Qn(d_ff_8_qn), .en(1'b1));  // open: preset, reset
endmodule

module CPU_Control (
  input  Clock,
  input  [3:0] Opcode,
  input  Zero,
  input  Minus,
  input  Carry,
  output PC_Src_MUX,
  output PC_Write,
  output IR_Write,
  output Data_Write,
  output [1:0] Acc_Src_MUX,
  output Acc_Write,
  output Write,
  output Address_Src_MUX,
  output PC_Src_MUX_High,
  output Read
);

  wire [3:0] rom_1_data;
  wire [7:4] State_q;
  wire [15:11] rom_2_data;

  Register #(.width(4)) State (.D(rom_1_data), .Q(State_q), .clk(Clock));  // open: en, clr
  ROM #(.addrWidth(16), .dataWidth(4)) rom_1 (
    .addr({{5{1'b0}}, Carry, Minus, Zero, State_q, Opcode}), .data(rom_1_data));  // open: sel
  ROM #(.addrWidth(4), .dataWidth(16)) rom_2 (
    .addr(State_q),
    .data({rom_2_data, Read, PC_Src_MUX_High, Address_Src_MUX, Write, Acc_Write, Acc_Src_MUX, Data_Write, IR_Write, PC_Write, PC_Src_MUX}));  // open: sel

  // Notes on the sheet:
  //   contents of rom_1 (hex, n*v repeats v):
  //   16*1 7*2 4 5 6 7 9 a 0 0 0 4*3 4 4 4 83*0 8 133*0 16*1 7*2 4 5 6 7 9 a 9 0 0 4*3 4 4 4 83*0 8 133*0
  //   16*1 7*2 4 5 6 7 9 a 0 9 0 4*3 4 4 4 83*0 8 133*0 16*1 7*2 4 5 6 7 9 a 9 9 0 4*3 4 4 4 83*0 8 133*0
  //   16*1 7*2 4 5 6 7 9 a 0 0 9 4*3 4 4 4 83*0 8 133*0 16*1 7*2 4 5 6 7 9 a 9 0 9 4*3 4 4 4 83*0 8 133*0
  //   16*1 7*2 4 5 6 7 9 a 0 9 9 4*3 4 4 4 83*0 8 133*0 16*1 7*2 4 5 6 7 9 a 9 9 9 4*3 4 4 4 83*0 8
  //   contents of rom_2 (hex, n*v repeats v):
  //   407 0 508 60 60 40 550 100 180 2 702
endmodule

module Port_Select_fromRange (
  input  [11:0] Address_Bus,
  input  [11:0] Range_LOW,
  input  [11:0] Range_HIGH,
  output Select
);

  wire comparator_1_eq, comparator_1_gt, comparator_2_eq, comparator_2_lt, or_1_out, or_2_out;

  or or_1 (or_1_out, comparator_1_eq, comparator_1_gt);
  Comparator #(.width(12), .mode("unsigned")) comparator_1 (
    .a(Address_Bus), .b(Range_LOW), .gt(comparator_1_gt), .eq(comparator_1_eq));  // open: lt
  and and_1 (Select, or_1_out, or_2_out);
  or or_2 (or_2_out, comparator_2_eq, comparator_2_lt);
  Comparator #(.width(12), .mode("unsigned")) comparator_2 (
    .a(Address_Bus), .b(Range_HIGH), .eq(comparator_2_eq), .lt(comparator_2_lt));  // open: gt
endmodule

module Real_Time_Clock (
  input  Clock,
  input  [15:0] SetSeconds,
  input  [15:0] SetMinutes,
  input  [15:0] SetHours,
  input  Set,
  output [15:0] Hours,
  output [15:0] Minutes,
  output [15:0] Seconds
);

  wire Clockrate_Divider_carry, counter_2_carry, counter_3_carry, not_1_out, not_2_out, not_3_out;

  Counter #(.width(16), .max('hffff)) counter_1 (
    .load(Set), .D(SetHours), .count(not_3_out), .Q(Hours), .clk(not_1_out));  // open: carry, clr
  Counter #(.width(16), .max('h3b)) counter_2 (
    .load(Set), .D(SetMinutes), .count(not_3_out), .Q(Minutes), .carry(counter_2_carry), .clk(not_2_out));  // open: clr
  not not_1 (not_1_out, counter_2_carry);
  Counter #(.width(32), .max('hc8)) Clockrate_Divider (
    .carry(Clockrate_Divider_carry), .clk(Clock));  // open: load, D, count, Q, clr
  Counter #(.width(16), .max('h3b)) counter_3 (
    .load(Set), .D(SetSeconds), .count(not_3_out), .Q(Seconds), .carry(counter_3_carry),
    .clk(Clockrate_Divider_carry));  // open: clr
  not not_2 (not_2_out, counter_3_carry);
  not not_3 (not_3_out, Set);
endmodule

module APP_DotMover (
  input  Read,
  input  Write,
  input  [15:0] Data_In,
  input  [11:0] Address_Bus,
  input  [11:0] Ports_Address,
  output out_6,
  output [15:0] Data_Out
);

  wire [15:0] controlled_buffer_1_out, input_port_1_data_bus, output_port_1_data_out, rom_1_data;

  Output_Port output_port_1 (
    .Data_Out(output_port_1_data_out), .Write(Write), .Address_Bus(Address_Bus),
    .Port_s_Address(Ports_Address), .Data_Bus(controlled_buffer_1_out));  // open: Write_Enable
  assign controlled_buffer_1_out = Write ? Data_In : 16'bz;  // Controlled_Buffer controlled_buffer_1
  assign Data_Out = Read ? input_port_1_data_bus : 16'bz;  // Controlled_Buffer controlled_buffer_2
  ROM #(.addrWidth(10), .dataWidth(16)) rom_1 (.addr(output_port_1_data_out[9:0]), .data(rom_1_data));  // open: sel
  Input_Port input_port_1 (
    .Data_Bus(input_port_1_data_bus), .Read(Read), .Address_Bus(Address_Bus), .Port_s_Address(Ports_Address),
    .Data_In(rom_1_data));

  assign out_6 = 1'b1;

  // Notes on the sheet:
  //   contents of rom_1 (hex, n*v repeats v):
  //   b9 50 69 78 65 6c 20 4d 6f 76 65 72 0 b066 8000 8000 1 3 1 3 57 65 6c 63 6f 6d 65 20 74 6f 20 50 69
  //   78 65 6c 20 4d 6f 76 65 72 21 20 50 72 65 73 73 20 71 75 69 74 20 74 6f 20 71 75 69 74 2e 0 55 73 65
  //   20 74 68 65 20 6a 6f 79 73 74 69 63 6b 20 74 6f 20 63 6f 6e 74 72 6f 6c 20 74 68 65 20 70 69 78 65
  //   6c 2e 0 47 6f 6f 64 62 79 65 21 0 0 0 9409 ac02 8008 a8bb 806d a8bc b8bd 8073 a8bb 8072 a8bc b8bd
  //   b485 8034 a8bb 8078 a8bc b8bd 807e a8bb 807d a8bc b8bd b485 9c09 6450 d0a9 9c00 a065 9c01 a064 6007
  //   d095 9064 6006 d09a 9065 6005 d09f 9065 6004 d0a4 9003 ac00 9002 ac01 b07e 9003 ac08 9c08 a003 b087
  //   9003 ac07 9c07 a003 b08a 9002 ac08 9c08 a002 b08d 9002 ac07 9c07 a002 b090 805b a8bb 80ae a8bc b8bd
  //   80b4 a8bb 80b3 a8bc b8bd b485 80b7 a8bc b8c7 a8cf c8cf 1 0 0 98bb abff 98be 28ba a8be 98cd 28ba a8cd
  //   98bb c8bc 98be 8ba a8be 98cd 8ba a8cd 9bff c8bc 0 b000
endmodule

module APP_HelloWorld (
  input  Read,
  input  Write,
  input  [15:0] Data_In,
  input  [11:0] Address_Bus,
  input  [11:0] Ports_Address,
  output out_6,
  output [15:0] Data_Out
);

  wire [15:0] controlled_buffer_1_out, input_port_1_data_bus, output_port_1_data_out, rom_1_data;

  Output_Port output_port_1 (
    .Data_Out(output_port_1_data_out), .Write(Write), .Address_Bus(Address_Bus),
    .Port_s_Address(Ports_Address), .Data_Bus(controlled_buffer_1_out));  // open: Write_Enable
  assign controlled_buffer_1_out = Write ? Data_In : 16'bz;  // Controlled_Buffer controlled_buffer_1
  assign Data_Out = Read ? input_port_1_data_bus : 16'bz;  // Controlled_Buffer controlled_buffer_2
  ROM #(.addrWidth(10), .dataWidth(16)) rom_1 (.addr(output_port_1_data_out[9:0]), .data(rom_1_data));  // open: sel
  Input_Port input_port_1 (
    .Data_Bus(input_port_1_data_bus), .Read(Read), .Address_Bus(Address_Bus), .Port_s_Address(Ports_Address),
    .Data_In(rom_1_data));

  assign out_6 = 1'b1;

  // Notes on the sheet:
  //   contents of rom_1 (hex, n*v repeats v):
  //   1f 48 65 6c 6c 6f 20 57 6f 72 6c 64 0 b00f 48 65 6c 6c 6f 20 57 6f 72 6c 64 21 0 8002 a8bb 8014 a8bc
  //   b8bd 801a a8bb 8019 a8bc b8bd b485 801d a8bc b8c7 a8cf c8cf 1 0 0 98bb abff 98be 28ba a8be 98cd 28ba
  //   a8cd 98bb c8bc 98be 8ba a8be 98cd 8ba a8cd 9bff c8bc 0 b000 0 b000
endmodule

module APP_SpaceInvaders (
  input  Read,
  input  Write,
  input  [15:0] Data_In,
  input  [11:0] Address_Bus,
  input  [11:0] Ports_Address,
  output out_6,
  output [15:0] Data_Out
);

  wire [15:0] controlled_buffer_1_out, input_port_1_data_bus, output_port_1_data_out, rom_1_data;

  Output_Port output_port_1 (
    .Data_Out(output_port_1_data_out), .Write(Write), .Address_Bus(Address_Bus),
    .Port_s_Address(Ports_Address), .Data_Bus(controlled_buffer_1_out));  // open: Write_Enable
  assign controlled_buffer_1_out = Write ? Data_In : 16'bz;  // Controlled_Buffer controlled_buffer_1
  assign Data_Out = Read ? input_port_1_data_bus : 16'bz;  // Controlled_Buffer controlled_buffer_2
  ROM #(.addrWidth(10), .dataWidth(16)) rom_1 (.addr(output_port_1_data_out[9:0]), .data(rom_1_data));  // open: sel
  Input_Port input_port_1 (
    .Data_Bus(input_port_1_data_bus), .Read(Read), .Address_Bus(Address_Bus), .Port_s_Address(Ports_Address),
    .Data_In(rom_1_data));

  assign out_6 = 1'b1;

  // Notes on the sheet:
  //   contents of rom_1 (hex, n*v repeats v):
  //   138 53 70 61 63 65 20 49 6e 76 61 64 65 72 73 0 b08c 57 65 6c 63 6f 6d 65 20 74 6f 20 53 70 61 63 65
  //   20 49 6e 76 61 64 65 72 73 21 0 4c 6f 61 64 69 6e 67 2e 2e 2e 0 44 6f 6e 65 21 0 50 72 65 73 73 20
  //   51 55 49 54 20 74 6f 20 71 75 69 74 20 74 68 65 20 67 61 6d 65 0 41 72 65 20 79 6f 75 20 73 75 72 65
  //   20 79 6f 75 20 77 6f 75 6c 64 20 6c 69 6b 65 20 74 6f 20 71 75 69 74 3f 0 47 6f 6f 64 62 79 65 21
  //   14*0 80 1c0 0 0 1 3 1 8002 a987 8091 a988 b989 8097 a987 8096 a988 b989 b484 801d a987 809c a988
  //   b989 80a2 a987 80a1 a988 b989 b484 8078 a987 80a7 a988 b989 80ad a987 80ac a988 b989 b91a 80b3 a987
  //   80b2 a988 b989 b8fc 8028 a987 80b8 a988 b989 80be a987 80bd a988 b989 b484 802e a987 80c3 a988 b989
  //   80c9 a987 80c8 a988 b989 b484 8001 a08b 9c09 644d d100 9c00 a088 6089 d0de 9088 608a d0ef d08b b0c9
  //   80dd a987 80dc a988 b989 b8fc b0d5 940e ac07 9c07 a40e 940f ac07 9c07 a40f 800d ac00 940e ac01 800e
  //   ac00 940f ac01 b0d2 940e ac08 9c08 a40e 940f ac08 9c08 a40f 800d ac00 940e ac01 800e ac00 940f ac01
  //   b0d5 804a a987 8105 a988 b989 810b a987 810a a988 b989 b93a 810e a988 b993 d110 b0ce 806f a987 8115
  //   a988 b989 811b a987 811a a988 b989 b484 8401 a987 8120 a988 b989 8010 a987 8125 a988 b989 812b a987
  //   812a a988 b989 b5f4 8131 a987 8130 a988 b989 b8fc 9419 ac02 8136 a988 b993 a99b c99b 1 0 0 9987 abff
  //   998a 2986 a98a 9999 2986 a999 9987 c988 998a 986 a98a 9999 986 a999 9bff c988 0 b000
endmodule

module ProgramDockController (
  input  Read,
  input  Write,
  input  [15:0] Data_In,
  input  [11:0] Address_Bus,
  input  [15:0] Data_Out,
  input  in_6,
  output out_7,
  output out_8,
  output [15:0] Data_Out_2,
  output Read_2,
  output Write_2,
  output [15:0] Data_In_2,
  output [11:0] Address_Bus_2,
  output [11:0] Ports_Address
);

  not not_1 (out_8, in_6);

  assign Address_Bus_2 = Address_Bus;
  assign Data_In_2 = Data_In;
  assign Data_Out_2 = Data_Out;
  assign out_7 = in_6;
  assign Ports_Address = 12'hc03;
  assign Read_2 = Read;
  assign Write_2 = Write;

  // Notes on the sheet:
  //   out_7: pull=down
  //   in_6: pull=down
  //   Data_Out_2: pull=down
endmodule

module _16x16_screen_controller (
  input  [15:0] Row_Data,
  input  [15:0] Row_Select,
  input  Write,
  output [15:0] Row,
  output [15:0] Row_2,
  output [15:0] Row_3,
  output [15:0] Row_4,
  output [15:0] Row_5,
  output [15:0] Row_6,
  output [15:0] Row_7,
  output [15:0] Row_8,
  output [15:0] Row_9,
  output [15:0] Row_10,
  output [15:0] Row_11,
  output [15:0] Row_12,
  output [15:0] Row_13,
  output [15:0] Row_14,
  output [15:0] Row_15,
  output [15:0] Row_16
);

  wire decoder_1_out0, decoder_1_out1, decoder_1_out2, decoder_1_out3, decoder_1_out4, decoder_1_out5,
       decoder_1_out6, decoder_1_out7, decoder_1_out8, decoder_1_out9, decoder_1_out10, decoder_1_out11,
       decoder_1_out12, decoder_1_out13, decoder_1_out14, decoder_1_out15;

  Decoder #(.select(4), .enable("false")) decoder_1 (
    .out0(decoder_1_out0), .out1(decoder_1_out1), .out2(decoder_1_out2), .out3(decoder_1_out3),
    .out4(decoder_1_out4), .out5(decoder_1_out5), .out6(decoder_1_out6), .out7(decoder_1_out7),
    .out8(decoder_1_out8), .out9(decoder_1_out9), .out10(decoder_1_out10), .out11(decoder_1_out11),
    .out12(decoder_1_out12), .out13(decoder_1_out13), .out14(decoder_1_out14), .out15(decoder_1_out15),
    .sel(Row_Select[3:0]));
  Register #(.width(16), .trigger("high")) register_1 (
    .D(Row_Data), .en(decoder_1_out0), .Q(Row), .clk(Write));  // open: clr
  Register #(.width(16), .trigger("high")) register_2 (
    .D(Row_Data), .en(decoder_1_out1), .Q(Row_2), .clk(Write));  // open: clr
  Register #(.width(16), .trigger("high")) register_3 (
    .D(Row_Data), .en(decoder_1_out2), .Q(Row_3), .clk(Write));  // open: clr
  Register #(.width(16), .trigger("high")) register_4 (
    .D(Row_Data), .en(decoder_1_out3), .Q(Row_4), .clk(Write));  // open: clr
  Register #(.width(16), .trigger("high")) register_5 (
    .D(Row_Data), .en(decoder_1_out4), .Q(Row_5), .clk(Write));  // open: clr
  Register #(.width(16), .trigger("high")) register_6 (
    .D(Row_Data), .en(decoder_1_out5), .Q(Row_6), .clk(Write));  // open: clr
  Register #(.width(16), .trigger("high")) register_7 (
    .D(Row_Data), .en(decoder_1_out6), .Q(Row_7), .clk(Write));  // open: clr
  Register #(.width(16), .trigger("high")) register_8 (
    .D(Row_Data), .en(decoder_1_out7), .Q(Row_8), .clk(Write));  // open: clr
  Register #(.width(16), .trigger("high")) register_9 (
    .D(Row_Data), .en(decoder_1_out8), .Q(Row_9), .clk(Write));  // open: clr
  Register #(.width(16), .trigger("high")) register_10 (
    .D(Row_Data), .en(decoder_1_out9), .Q(Row_10), .clk(Write));  // open: clr
  Register #(.width(16), .trigger("high")) register_11 (
    .D(Row_Data), .en(decoder_1_out10), .Q(Row_11), .clk(Write));  // open: clr
  Register #(.width(16), .trigger("high")) register_12 (
    .D(Row_Data), .en(decoder_1_out11), .Q(Row_12), .clk(Write));  // open: clr
  Register #(.width(16), .trigger("high")) register_13 (
    .D(Row_Data), .en(decoder_1_out12), .Q(Row_13), .clk(Write));  // open: clr
  Register #(.width(16), .trigger("high")) register_14 (
    .D(Row_Data), .en(decoder_1_out13), .Q(Row_14), .clk(Write));  // open: clr
  Register #(.width(16), .trigger("high")) register_15 (
    .D(Row_Data), .en(decoder_1_out14), .Q(Row_15), .clk(Write));  // open: clr
  Register #(.width(16), .trigger("high")) register_16 (
    .D(Row_Data), .en(decoder_1_out15), .Q(Row_16), .clk(Write));  // open: clr
endmodule

module SIMPLE_EXAMPLE (
);

  wire button_1_out, button_2_out, button_3_out, button_4_out, button_5_out, button_6_out, button_7_out,
       button_8_out, button_9_out, button_10_out, button_11_out, button_12_out, button_13_out, button_14_out,
       button_15_out, button_16_out, button_17_out, button_18_out, button_19_out, button_20_out,
       button_21_out, button_22_out, button_23_out, button_24_out, button_25_out, button_26_out,
       button_27_out, button_28_out, button_29_out, button_30_out, button_31_out, button_32_out, clock_1_out,
       cpu_1_read, cpu_1_write, not_1_out, not_2_out, not_3_out, port_select_fromrange_1_select,
       port_select_fromrange_2_select, undriven;
  wire [1:0] subtractor_1_out_2;
  wire [9:0] subtractor_1_out;
  wire [10:0] cpu_1_address_bus;
  wire [11:11] cpu_1_address_bus_2;
  wire [15:0] controlled_buffer_1_out, controlled_buffer_2_out, controlled_buffer_5_out, cpu_1_data_bus_out,
       n8_bit_toggle_array_1_o0, n8_bit_toggle_array_3_o0, output_port_1_data_out, rom_1_data;

  Clock clock_1 (.out(clock_1_out));
  CPU cpu_1 (
    .Read(cpu_1_read), .Write(cpu_1_write), .Clock(clock_1_out),
    .Address_Bus({cpu_1_address_bus_2[11], cpu_1_address_bus}), .Data_Bus_Out(cpu_1_data_bus_out),
    .Data_Bus_In(controlled_buffer_2_out));
  assign controlled_buffer_1_out = not_1_out ? cpu_1_data_bus_out : 16'bz;  // Controlled_Buffer controlled_buffer_1
  assign controlled_buffer_2_out = cpu_1_read ? controlled_buffer_1_out : 16'bz;  // Controlled_Buffer controlled_buffer_2
  not not_1 (not_1_out, cpu_1_read);
  Subtractor #(.width(12)) subtractor_1 (
    .a({cpu_1_address_bus_2[11], cpu_1_address_bus}), .b(12'h800),
    .out({subtractor_1_out_2, subtractor_1_out}));  // open: bin, bout
  Port_Select_fromRange port_select_fromrange_1 (
    .Select(port_select_fromrange_1_select), .Address_Bus({cpu_1_address_bus_2[11], cpu_1_address_bus}),
    .Range_LOW({12{1'b0}}), .Range_HIGH(12'h3ff));
  Port_Select_fromRange port_select_fromrange_2 (
    .Select(port_select_fromrange_2_select), .Address_Bus({cpu_1_address_bus_2[11], cpu_1_address_bus}),
    .Range_LOW(12'h400), .Range_HIGH(12'hbff));
  ROM #(.addrWidth(11), .dataWidth(16)) rom_1 (
    .addr(cpu_1_address_bus), .data(rom_1_data), .sel(port_select_fromrange_1_select));
  assign rom_1_data = not_2_out ? controlled_buffer_1_out : 16'bz;  // Controlled_Buffer controlled_buffer_3
  assign controlled_buffer_1_out = cpu_1_read ? rom_1_data : 16'bz;  // Controlled_Buffer controlled_buffer_4
  assign controlled_buffer_5_out = not_3_out ? controlled_buffer_1_out : 16'bz;  // Controlled_Buffer controlled_buffer_5
  RAM #(.addrWidth(10), .dataWidth(16)) ram_1 (
    .addr(subtractor_1_out), .data(controlled_buffer_5_out), .sel(port_select_fromrange_2_select),
    .clk(cpu_1_write), .ld(cpu_1_read), .clr(undriven));
  not not_2 (not_2_out, cpu_1_read);
  assign controlled_buffer_1_out = cpu_1_read ? controlled_buffer_5_out : 16'bz;  // Controlled_Buffer controlled_buffer_6
  not not_3 (not_3_out, cpu_1_read);
  Button button_1 (.out(button_1_out));
  Button button_2 (.out(button_2_out));
  Button button_3 (.out(button_3_out));
  Button button_4 (.out(button_4_out));
  Button button_5 (.out(button_5_out));
  Button button_6 (.out(button_6_out));
  Button button_7 (.out(button_7_out));
  Button button_8 (.out(button_8_out));
  Button button_9 (.out(button_9_out));
  Button button_10 (.out(button_10_out));
  Button button_11 (.out(button_11_out));
  Button button_12 (.out(button_12_out));
  Button button_13 (.out(button_13_out));
  Button button_14 (.out(button_14_out));
  Button button_15 (.out(button_15_out));
  Button button_16 (.out(button_16_out));
  Input_Port input_port_1 (
    .Data_Bus(controlled_buffer_1_out), .Read(cpu_1_read),
    .Address_Bus({cpu_1_address_bus_2[11], cpu_1_address_bus}), .Port_s_Address(12'hc00),
    .Data_In(n8_bit_toggle_array_1_o0));
  _8_bit_Toggle_Array u_8_bit_toggle_array_1 (
    .I0(button_1_out), .I1(button_2_out), .I2(button_3_out), .I3(button_4_out), .I4(button_5_out),
    .I5(button_6_out), .I6(button_7_out), .I7(button_8_out), .O0(n8_bit_toggle_array_1_o0[0]),
    .O1(n8_bit_toggle_array_1_o0[1]), .O2(n8_bit_toggle_array_1_o0[2]), .O3(n8_bit_toggle_array_1_o0[3]),
    .O4(n8_bit_toggle_array_1_o0[4]), .O5(n8_bit_toggle_array_1_o0[5]), .O6(n8_bit_toggle_array_1_o0[6]),
    .O7(n8_bit_toggle_array_1_o0[7]));
  _8_bit_Toggle_Array u_8_bit_toggle_array_2 (
    .I0(button_9_out), .I1(button_10_out), .I2(button_11_out), .I3(button_12_out), .I4(button_13_out),
    .I5(button_14_out), .I6(button_15_out), .I7(button_16_out), .O0(n8_bit_toggle_array_1_o0[8]),
    .O1(n8_bit_toggle_array_1_o0[9]), .O2(n8_bit_toggle_array_1_o0[10]), .O3(n8_bit_toggle_array_1_o0[11]),
    .O4(n8_bit_toggle_array_1_o0[12]), .O5(n8_bit_toggle_array_1_o0[13]), .O6(n8_bit_toggle_array_1_o0[14]),
    .O7(n8_bit_toggle_array_1_o0[15]));
  DotMatrix #(.inputtype("row"), .matrixcols(16), .matrixrows(1), .dotshape("circle")) dotmatrix_1 (.row0(n8_bit_toggle_array_1_o0));
  DotMatrix #(.inputtype("row"), .matrixcols(16), .matrixrows(1), .dotshape("circle")) dotmatrix_2 (.row0(output_port_1_data_out));
  Output_Port output_port_1 (
    .Data_Out(output_port_1_data_out), .Write(cpu_1_write),
    .Address_Bus({cpu_1_address_bus_2[11], cpu_1_address_bus}), .Port_s_Address(12'hc00),
    .Data_Bus(controlled_buffer_1_out));  // open: Write_Enable
  Button button_17 (.out(button_17_out));
  Button button_18 (.out(button_18_out));
  Button button_19 (.out(button_19_out));
  Button button_20 (.out(button_20_out));
  Button button_21 (.out(button_21_out));
  Button button_22 (.out(button_22_out));
  Button button_23 (.out(button_23_out));
  Button button_24 (.out(button_24_out));
  Button button_25 (.out(button_25_out));
  Button button_26 (.out(button_26_out));
  Button button_27 (.out(button_27_out));
  Button button_28 (.out(button_28_out));
  Button button_29 (.out(button_29_out));
  Button button_30 (.out(button_30_out));
  Button button_31 (.out(button_31_out));
  Button button_32 (.out(button_32_out));
  Input_Port input_port_2 (
    .Data_Bus(controlled_buffer_1_out), .Read(cpu_1_read),
    .Address_Bus({cpu_1_address_bus_2[11], cpu_1_address_bus}), .Port_s_Address(12'hc01),
    .Data_In(n8_bit_toggle_array_3_o0));
  DotMatrix #(.inputtype("row"), .matrixcols(16), .matrixrows(1), .dotshape("circle")) dotmatrix_3 (.row0(n8_bit_toggle_array_3_o0));
  _8_bit_Toggle_Array u_8_bit_toggle_array_3 (
    .I0(button_17_out), .I1(button_18_out), .I2(button_19_out), .I3(button_20_out), .I4(button_21_out),
    .I5(button_22_out), .I6(button_23_out), .I7(button_24_out), .O0(n8_bit_toggle_array_3_o0[0]),
    .O1(n8_bit_toggle_array_3_o0[1]), .O2(n8_bit_toggle_array_3_o0[2]), .O3(n8_bit_toggle_array_3_o0[3]),
    .O4(n8_bit_toggle_array_3_o0[4]), .O5(n8_bit_toggle_array_3_o0[5]), .O6(n8_bit_toggle_array_3_o0[6]),
    .O7(n8_bit_toggle_array_3_o0[7]));
  _8_bit_Toggle_Array u_8_bit_toggle_array_4 (
    .I0(button_25_out), .I1(button_26_out), .I2(button_27_out), .I3(button_28_out), .I4(button_29_out),
    .I5(button_30_out), .I6(button_31_out), .I7(button_32_out), .O0(n8_bit_toggle_array_3_o0[8]),
    .O1(n8_bit_toggle_array_3_o0[9]), .O2(n8_bit_toggle_array_3_o0[10]), .O3(n8_bit_toggle_array_3_o0[11]),
    .O4(n8_bit_toggle_array_3_o0[12]), .O5(n8_bit_toggle_array_3_o0[13]), .O6(n8_bit_toggle_array_3_o0[14]),
    .O7(n8_bit_toggle_array_3_o0[15]));

  // Notes on the sheet:
  //   CPU
  //   2K PROGRAM ROM
  //   1K RAM
  //   contents of rom_1 (hex, n*v repeats v):
  //   b002 1 8000 a802 9c00 a800 9c01 a801 9800 d011 9802 801 a802 9800 2001 a800 b008 9802 ac00 b002
  //   INPUT (addr 0xC00)
  //   OUTPUT (addr 0xC00)
  //   INPUT (addr 0xC01)
  //   DATA BUS
  //   READ
  //   WRITE
  //   CLOCK
  //   ADDRESS BUS
endmodule
